// Logisim project DudziakMaksymilian.circ as structural Verilog: 1 circuit, main circuit main
module main (
  input  nCP0,
  output _1,
  output _2,
  output _4,
  output _8,
  output _16,
  output _32,
  output _64,
  output _128
);

  wire and_1_out, nand_1_out, nand_2_out, not_1_out, not_2_out, not_3_out, not_4_out, not_5_out, not_6_out,
       not_7_out, not_8_out;

  not not_1 (not_1_out, nand_1_out);
  J_K_Flip_Flop #(.trigger("falling")) Q0 (
    .J(1'b1), .clk(nCP0), .K(1'b1), .Q(_1), .reset(not_1_out));  // open: Qn, preset, en
  nand nand_1 (nand_1_out, _1, and_1_out);
  J_K_Flip_Flop #(.trigger("falling")) Q1 (
    .J(1'b1), .clk(_1), .K(1'b1), .Q(_2), .reset(not_2_out));  // open: Qn, preset, en
  not not_2 (not_2_out, nand_1_out);
  J_K_Flip_Flop #(.trigger("falling")) Q2 (
    .J(1'b1), .clk(_2), .K(1'b1), .Q(_4), .reset(not_3_out));  // open: Qn, preset, en
  not not_3 (not_3_out, nand_1_out);
  J_K_Flip_Flop #(.trigger("falling")) Q3 (
    .J(1'b1), .clk(_4), .K(1'b1), .Q(_8), .reset(not_4_out));  // open: Qn, preset, en
  not not_4 (not_4_out, nand_1_out);
  and and_1 (and_1_out, _4, _128, _16);
  J_K_Flip_Flop #(.trigger("falling")) Q0_2 (
    .J(1'b1), .clk(_8), .K(1'b1), .Q(_16), .reset(not_5_out));  // open: Qn, preset, en
  not not_5 (not_5_out, nand_2_out);
  nand nand_2 (nand_2_out, _1, and_1_out);
  J_K_Flip_Flop #(.trigger("falling")) Q1_2 (
    .J(1'b1), .clk(_16), .K(1'b1), .Q(_32), .reset(not_6_out));  // open: Qn, preset, en
  not not_6 (not_6_out, nand_2_out);
  not not_7 (not_7_out, nand_2_out);
  J_K_Flip_Flop #(.trigger("falling")) Q2_2 (
    .J(1'b1), .clk(_32), .K(1'b1), .Q(_64), .reset(not_7_out));  // open: Qn, preset, en
  J_K_Flip_Flop #(.trigger("falling")) Q3_2 (
    .J(1'b1), .clk(_64), .K(1'b1), .Q(_128), .reset(not_8_out));  // open: Qn, preset, en
  not not_8 (not_8_out, nand_2_out);

  // Notes on the sheet:
  //   Modulo 149
  //   /CP1
  //   MR1
  //   MR2
  //   /CP0
  //   /CP1
  //   MR1
  //   MR2
endmodule
