// Logisim project DudziakMaksymilianALU.circ as structural Verilog: 1 circuit, main circuit main
module main (
  input  c0,
  input  b0,
  input  a0,
  input  b1,
  input  a1,
  input  [1:0] f,
  output out_7,
  output out_8,
  output ALU0,
  output out_10,
  output out_11,
  output out_12,
  output out_13,
  output ALU1,
  output out_15,
  output out_16,
  output c1
);

  wire and_2_out, and_3_out, and_5_out, and_6_out, C0_out;

  xor \xor  (out_8, b0, a0);
  nor \nor  (out_10, b0, a0);
  and \and  (out_11, a0, b0);
  and and_2 (and_2_out, a0, c0);
  and and_3 (and_3_out, b0, c0);
  xor xor_2 (out_13, b1, a1);
  nor nor_2 (out_15, b1, a1);
  and and_4 (out_16, a1, b1);
  and and_5 (and_5_out, a1, C0_out);
  and and_6 (and_6_out, b1, C0_out);
  xor S0 (out_7, c0, out_8);
  or u_C0 (C0_out, out_11, and_2_out, and_3_out);
  xor S1 (out_12, C0_out, out_13);
  or u_C1 (c1, out_16, and_5_out, and_6_out);
  Multiplexer #(.select(2)) multiplexer_1 (
    .in0(out_7), .in1(out_8), .in2(out_10), .in3(out_11), .out(ALU0), .sel(f));  // open: en
  Multiplexer #(.select(2)) multiplexer_2 (
    .in0(out_12), .in1(out_13), .in2(out_15), .in3(out_16), .out(ALU1), .sel(f));  // open: en
endmodule
