// Logisim project DudziakMaksymilianBCD.circ as structural Verilog: 1 circuit, main circuit main
module main (
  input  [3:0] in_1
);

  wire A_out, B_out, C_out, D_out, decoder_1_out0, decoder_1_out1, decoder_1_out2, decoder_1_out3,
       decoder_1_out4, decoder_1_out5, decoder_1_out6, decoder_1_out7, decoder_1_out8, decoder_1_out9, E_out,
       F_out, G_out;

  Decoder #(.select(4)) decoder_1 (
    .out0(decoder_1_out0), .out1(decoder_1_out1), .out2(decoder_1_out2), .out3(decoder_1_out3),
    .out4(decoder_1_out4), .out5(decoder_1_out5), .out6(decoder_1_out6), .out7(decoder_1_out7),
    .out8(decoder_1_out8), .out9(decoder_1_out9), .sel(in_1));  // open: out10, out11, out12, out13, out14, out15, en
  or B (B_out, decoder_1_out1, decoder_1_out2, decoder_1_out3, decoder_1_out4, decoder_1_out7, decoder_1_out8, decoder_1_out9, decoder_1_out0);
  or A (A_out, decoder_1_out2, decoder_1_out3, decoder_1_out5, decoder_1_out6, decoder_1_out7, decoder_1_out8, decoder_1_out9, decoder_1_out0);
  or G (G_out, decoder_1_out3, decoder_1_out4, decoder_1_out5, decoder_1_out2, decoder_1_out6, decoder_1_out8, decoder_1_out9);
  or E (E_out, decoder_1_out8, decoder_1_out0, decoder_1_out2, decoder_1_out6);
  or D (D_out, decoder_1_out3, decoder_1_out5, decoder_1_out6, decoder_1_out2, decoder_1_out8, decoder_1_out9, decoder_1_out0);
  or C (C_out, decoder_1_out1, decoder_1_out3, decoder_1_out4, decoder_1_out5, decoder_1_out0, decoder_1_out6, decoder_1_out7, decoder_1_out8, decoder_1_out9);
  or F (F_out, decoder_1_out5, decoder_1_out6, decoder_1_out8, decoder_1_out9, decoder_1_out0, decoder_1_out4);
  _7_Segment_Display u_7_segment_display_1 (
    .g(G_out), .f(F_out), .a(A_out), .b(B_out), .e(E_out), .d(D_out), .c(C_out));  // open: dp
endmodule
