// Logisim project DudziakMaksymilianDEK.circ as structural Verilog: 1 circuit, main circuit main
module main (
  input  c,
  input  b,
  input  a,
  input  nE1,
  input  nE2,
  input  E3,
  output out_7,
  output out_8,
  output out_9,
  output out_10,
  output out_11,
  output out_12,
  output out_13,
  output out_14
);

  wire and_1_out, not_1_out, not_2_out, not_3_out, not_4_out, not_5_out, not_6_out;

  and and_1 (and_1_out, ~nE1, ~nE2, E3);  // AND_Gate
  not not_1 (not_1_out, c);
  not not_2 (not_2_out, not_1_out);
  not not_3 (not_3_out, b);
  not not_4 (not_4_out, not_3_out);
  not not_5 (not_5_out, a);
  not not_6 (not_6_out, not_5_out);
  nand nY0 (out_7, not_5_out, not_3_out, not_1_out, and_1_out);
  nand nY1 (out_8, not_6_out, not_3_out, not_1_out, and_1_out);
  nand nY2 (out_9, not_5_out, not_4_out, not_1_out, and_1_out);
  nand nY3 (out_10, not_6_out, not_4_out, not_1_out, and_1_out);
  nand nY4 (out_11, not_5_out, not_3_out, not_2_out, and_1_out);
  nand nY5 (out_12, not_6_out, not_3_out, not_2_out, and_1_out);
  nand nY6 (out_13, not_5_out, not_4_out, not_2_out, and_1_out);
  nand nY7 (out_14, not_6_out, not_4_out, not_2_out, and_1_out);
endmodule
