// Logisim project DudziakMaksymilianKBD.circ as structural Verilog: 1 circuit, main circuit main
module main (
  input  nWR,
  input  nIORQ,
  input  nRD,
  input  keyboard,
  input  D3,
  input  D2,
  input  D1,
  input  D0,
  input  in_9,
  input  in_10,
  input  in_11,
  input  in_12,
  input  in_13,
  input  in_14,
  input  in_15,
  input  in_16,
  input  in_17,
  input  in_18,
  input  in_19,
  input  in_20,
  input  in_21,
  input  in_22,
  input  in_23,
  input  in_24,
  output D3_2,
  output D2_2,
  output D1_2,
  output D0_2
);

  wire and_1_out, and_2_out, buffer_1_out, buffer_2_out, buffer_3_out, buffer_4_out, nor_1_out, nor_2_out,
       transistor_1_out, transistor_2_out, transistor_3_out, transistor_4_out;
  wire [3:0] RE_q;

  nor nor_1 (nor_1_out, nWR, nIORQ);
  nor nor_2 (nor_2_out, nIORQ, nRD);
  and and_1 (and_1_out, nor_2_out, keyboard);
  Register #(.width(4)) RE (.D({D3, D2, D1, D0}), .Q(RE_q), .clk(and_2_out));  // open: en, clr
  buf buffer_1 (buffer_1_out, RE_q[0]);
  Transistor transistor_1 (.in(buffer_1_out), .out(transistor_1_out), .gate(in_9));
  assign D3_2 = and_1_out ? transistor_1_out : 1'bz;  // Controlled_Buffer controlled_buffer_1
  Transistor transistor_2 (.in(buffer_1_out), .out(transistor_2_out), .gate(in_13));
  assign D2_2 = and_1_out ? transistor_2_out : 1'bz;  // Controlled_Buffer controlled_buffer_2
  Transistor transistor_3 (.in(buffer_1_out), .out(transistor_3_out), .gate(in_17));
  assign D1_2 = and_1_out ? transistor_3_out : 1'bz;  // Controlled_Buffer controlled_buffer_3
  Transistor transistor_4 (.in(buffer_1_out), .out(transistor_4_out), .gate(in_21));
  assign D0_2 = and_1_out ? transistor_4_out : 1'bz;  // Controlled_Buffer controlled_buffer_4
  and and_2 (and_2_out, keyboard, nor_1_out);
  buf buffer_2 (buffer_2_out, RE_q[1]);
  Transistor transistor_5 (.in(buffer_2_out), .out(transistor_1_out), .gate(in_10));
  Transistor transistor_6 (.in(buffer_2_out), .out(transistor_2_out), .gate(in_14));
  Transistor transistor_7 (.in(buffer_2_out), .out(transistor_3_out), .gate(in_18));
  Transistor transistor_8 (.in(buffer_2_out), .out(transistor_4_out), .gate(in_22));
  buf buffer_3 (buffer_3_out, RE_q[3]);
  buf buffer_4 (buffer_4_out, RE_q[2]);
  Transistor transistor_9 (.in(buffer_3_out), .out(transistor_1_out), .gate(in_12));
  Transistor transistor_10 (.in(buffer_4_out), .out(transistor_1_out), .gate(in_11));
  Transistor transistor_11 (.in(buffer_4_out), .out(transistor_2_out), .gate(in_15));
  Transistor transistor_12 (.in(buffer_3_out), .out(transistor_2_out), .gate(in_16));
  Transistor transistor_13 (.in(buffer_4_out), .out(transistor_3_out), .gate(in_19));
  Transistor transistor_14 (.in(buffer_3_out), .out(transistor_3_out), .gate(in_20));
  Transistor transistor_15 (.in(buffer_4_out), .out(transistor_4_out), .gate(in_23));
  Transistor transistor_16 (.in(buffer_3_out), .out(transistor_4_out), .gate(in_24));
  Pull_Resistor #(.pull(1)) pull_resistor_1 (.node(transistor_1_out));
  Pull_Resistor #(.pull(1)) pull_resistor_2 (.node(transistor_2_out));
  Pull_Resistor #(.pull(1)) pull_resistor_3 (.node(transistor_3_out));
  Pull_Resistor #(.pull(1)) pull_resistor_4 (.node(transistor_4_out));

  // Notes on the sheet:
  //   selected
  //   KBDRD
  //   buffer_1 drives only 0 and floats otherwise
  //   KBDWR
  //   buffer_2 drives only 0 and floats otherwise
  //   buffer_3 drives only 0 and floats otherwise
  //   buffer_4 drives only 0 and floats otherwise
  //   0/floating
endmodule
