// Logisim project DudziakMaksymilianLogicGates.circ as structural Verilog: 1 circuit, main circuit main
// 0 0 0 1
module main (
  input  c,
  input  b,
  input  a,
  output out_4,
  output out_5,
  output out_6
);

  wire and_1_out, nand_1_out, nand_2_out, nand_3_out, nand_4_out, nand_5_out, nand_6_out, nand_7_out,
       nand_8_out, nand_9_out, nor_1_out, nor_2_out, nor_3_out, nor_4_out, nor_5_out, nor_6_out, nor_7_out,
       nor_8_out, nor_9_out, nor_10_out, nor_11_out;

  nor nor_1 (nor_1_out, a, a);
  nor nor_2 (nor_2_out, b, b);
  nor nor_3 (nor_3_out, c, c);
  nand nand_1 (nand_1_out, a, a);
  nand nand_2 (nand_2_out, b, b);
  nor nor_4 (nor_4_out, a, b);
  nor nor_5 (nor_5_out, nor_4_out, nor_4_out);
  nor nor_6 (nor_6_out, nor_7_out, nor_7_out);
  nor nor_7 (nor_7_out, nor_1_out, nor_2_out);
  nand nand_3 (nand_3_out, nand_1_out, nand_2_out);
  nand nand_4 (nand_4_out, a, b);
  nor nor_8 (nor_8_out, a, b, c);
  and and_1 (and_1_out, a, b, c);
  nor nor_9 (nor_9_out, nor_5_out, c);
  nor nor_10 (nor_10_out, nor_6_out, nor_3_out);
  nand nand_5 (nand_5_out, nand_3_out, nand_3_out);
  nand nand_6 (nand_6_out, nand_5_out, nand_7_out);
  nand nand_7 (nand_7_out, c, c);
  nand nand_8 (nand_8_out, nand_4_out, nand_4_out);
  nand nand_9 (nand_9_out, nand_8_out, c);
  or or_1 (out_4, nor_8_out, and_1_out);
  nor nor_11 (nor_11_out, nor_9_out, nor_10_out);
  nand nand_10 (out_6, nand_6_out, nand_9_out);
  nor nor_12 (out_5, nor_11_out, nor_11_out);

  // Notes on the sheet:
  //   Numer zestawu = 897
  //    c b a Q
  //   0 0 0 1
  //   0 0 1 0
  //   0 1 0 0
  //   0 1 1 0
  //   1 0 0 0
  //   1 0 1 0
  //   1 1 0 0
  //   1 1 1 1
endmodule
